// Logisim project capstone-circuit.circ as structural Verilog: 11 circuits, main circuit main
module main (
  input  WE,
  output [7:0] IR_Current_Instruction,
  output CF,
  output SF,
  output ZF
);

  wire control_store_1_out_11;
  wire [1:0] control_store_1_r1, control_store_1_r2;
  wire [5:0] control_store_1_output;
  wire [7:0] alu_1_result, control_store_1__8_bit_imm_value, multiplexer_1_out, multiplexer_2_out,
       multiplexer_3_out, register_file_1_data_out_0, register_file_1_data_out_1;

  Multiplexer #(.width(8), .enable("false")) multiplexer_1 (
    .in1(alu_1_result), .out(multiplexer_1_out));  // open: in0, sel
  Register_File register_file_1 (
    .WE(WE), .Data_In(multiplexer_1_out), .Data_Out_0(register_file_1_data_out_0),
    .Data_Out_1(register_file_1_data_out_1), .Sw(control_store_1_r1), .Sr0(control_store_1_r1),
    .Sr1(control_store_1_r2));  // open: in_6
  Control_Store control_store_1 (
    .Current_Addr(IR_Current_Instruction), ._8_bit_imm_value(control_store_1__8_bit_imm_value),
    .r1(control_store_1_r1), .r2(control_store_1_r2), .out_11(control_store_1_out_11),
    .Output(control_store_1_output));  // open: Clear, Enable, Clock, Chip_Select, Clock_2, Load_Data, _8_bit_inst, Clear_2
  Multiplexer #(.width(8)) multiplexer_2 (
    .in0(register_file_1_data_out_0), .in1(control_store_1__8_bit_imm_value), .out(multiplexer_2_out),
    .sel(control_store_1_out_11));  // open: en
  Multiplexer #(.width(8)) multiplexer_3 (
    .in0(register_file_1_data_out_1), .in1(control_store_1__8_bit_imm_value), .out(multiplexer_3_out),
    .sel(control_store_1_out_11));  // open: en
  ALU alu_1 (
    .CF(CF), .A(multiplexer_2_out), .B(multiplexer_3_out), .Opcode(control_store_1_output),
    .Result(alu_1_result), .ZF(ZF), .SF(SF));
endmodule

module Logical_Unit (
  input  in_1,
  input  in_2,
  input  in_3,
  input  in_4,
  input  in_5,
  output out_6,
  output out_7,
  output out_8,
  output out_9,
  output out_10
);

  wire A___B_out, AB_out, Not_B_out;

  and AB (AB_out, in_1, in_2);
  or A___B (A___B_out, in_1, in_2);
  not Not_B (Not_B_out, in_2);
  and and_1 (out_6, AB_out, in_3);
  and and_2 (out_7, A___B_out, in_4);
  and and_3 (out_8, Not_B_out, in_5);

  assign out_9 = in_1;
  assign out_10 = in_2;
endmodule

module Full_Adder (
  input  in_1,
  input  in_2,
  input  in_3,
  input  in_4,
  output out_5,
  output out_6
);

  wire and_1_out, and_2_out, xor_1_out, xor_2_out;

  and and_1 (and_1_out, in_4, in_3, in_2);
  or or_1 (out_6, and_1_out, and_2_out);
  xor xor_1 (xor_1_out, in_2, in_3);
  and and_2 (and_2_out, in_4, xor_1_out, in_1);
  xor xor_2 (xor_2_out, in_1, xor_1_out);
  and and_3 (out_5, xor_2_out, in_4);
endmodule

module Decoder (
  input  in_1,
  input  in_2,
  output out_3,
  output out_4,
  output out_5,
  output out_6
);

  wire not_1_out, not_2_out;

  not not_1 (not_1_out, in_1);
  not not_2 (not_2_out, in_2);
  and and_1 (out_3, not_1_out, not_2_out);
  and and_2 (out_4, not_1_out, in_2);
  and and_3 (out_5, in_1, not_2_out);
  and and_4 (out_6, in_1, in_2);
endmodule

module _1bit_ALU (
  input  INVA,
  input  A,
  input  Carry_In,
  input  ENA,
  input  B,
  input  ENB,
  input  F0,
  input  F1,
  output Output,
  output Carry_Out
);

  wire and_1_out, and_2_out, DC_out_3, DC_out_4, DC_out_5, DC_out_6, FA_out_5, LU_out_6, LU_out_7, LU_out_8,
       LU_out_9, LU_out_10, xor_1_out;

  and and_1 (and_1_out, A, ENA);
  xor xor_1 (xor_1_out, INVA, and_1_out);
  and and_2 (and_2_out, B, ENB);
  Logical_Unit LU (
    .in_1(xor_1_out), .in_2(and_2_out), .out_6(LU_out_6), .out_7(LU_out_7), .out_8(LU_out_8),
    .out_9(LU_out_9), .out_10(LU_out_10), .in_3(DC_out_3), .in_4(DC_out_4), .in_5(DC_out_5));
  Decoder DC (.out_3(DC_out_3), .out_4(DC_out_4), .out_5(DC_out_5), .out_6(DC_out_6), .in_1(F0), .in_2(F1));
  Full_Adder FA (
    .in_2(LU_out_10), .in_3(LU_out_9), .in_4(DC_out_6), .in_1(Carry_In), .out_5(FA_out_5), .out_6(Carry_Out));
  or or_1 (Output, LU_out_6, LU_out_7, LU_out_8, FA_out_5);
endmodule

module ALU (
  input  [5:0] Opcode,
  input  [7:0] A,
  input  [7:0] B,
  output [7:0] Result,
  output SF,
  output ZF,
  output CF
);

  wire n1bit_alu_1_carry_out, n1bit_alu_2_carry_out, n1bit_alu_3_carry_out, n1bit_alu_4_carry_out,
       n1bit_alu_5_carry_out, n1bit_alu_6_carry_out, n1bit_alu_7_carry_out, not_1_out, not_2_out, not_3_out,
       not_4_out, not_5_out, not_6_out, not_7_out, not_8_out;

  _1bit_ALU u_1bit_alu_1 (
    .INVA(Opcode[1]), .A(A[0]), .ENA(Opcode[3]), .B(B[0]), .ENB(Opcode[2]), .F0(Opcode[5]), .F1(Opcode[4]),
    .Output(Result[0]), .Carry_Out(n1bit_alu_1_carry_out), .Carry_In(Opcode[0]));
  _1bit_ALU u_1bit_alu_2 (
    .INVA(Opcode[1]), .A(A[1]), .ENA(Opcode[3]), .B(B[1]), .ENB(Opcode[2]), .F0(Opcode[5]), .F1(Opcode[4]),
    .Output(Result[1]), .Carry_Out(n1bit_alu_2_carry_out), .Carry_In(n1bit_alu_1_carry_out));
  _1bit_ALU u_1bit_alu_3 (
    .INVA(Opcode[1]), .A(A[2]), .ENA(Opcode[3]), .B(B[2]), .ENB(Opcode[2]), .F0(Opcode[5]), .F1(Opcode[4]),
    .Output(Result[2]), .Carry_Out(n1bit_alu_3_carry_out), .Carry_In(n1bit_alu_2_carry_out));
  _1bit_ALU u_1bit_alu_4 (
    .INVA(Opcode[1]), .A(A[3]), .ENA(Opcode[3]), .B(B[3]), .ENB(Opcode[2]), .F0(Opcode[5]), .F1(Opcode[4]),
    .Output(Result[3]), .Carry_Out(n1bit_alu_4_carry_out), .Carry_In(n1bit_alu_3_carry_out));
  _1bit_ALU u_1bit_alu_5 (
    .INVA(Opcode[1]), .A(A[4]), .ENA(Opcode[3]), .B(B[4]), .ENB(Opcode[2]), .F0(Opcode[5]), .F1(Opcode[4]),
    .Output(Result[4]), .Carry_Out(n1bit_alu_5_carry_out), .Carry_In(n1bit_alu_4_carry_out));
  _1bit_ALU u_1bit_alu_6 (
    .INVA(Opcode[1]), .A(A[5]), .ENA(Opcode[3]), .B(B[5]), .ENB(Opcode[2]), .F0(Opcode[5]), .F1(Opcode[4]),
    .Output(Result[5]), .Carry_Out(n1bit_alu_6_carry_out), .Carry_In(n1bit_alu_5_carry_out));
  _1bit_ALU u_1bit_alu_7 (
    .INVA(Opcode[1]), .A(A[6]), .ENA(Opcode[3]), .B(B[6]), .ENB(Opcode[2]), .F0(Opcode[5]), .F1(Opcode[4]),
    .Output(Result[6]), .Carry_Out(n1bit_alu_7_carry_out), .Carry_In(n1bit_alu_6_carry_out));
  _1bit_ALU u_1bit_alu_8 (
    .INVA(Opcode[1]), .A(A[7]), .ENA(Opcode[3]), .B(B[7]), .ENB(Opcode[2]), .F0(Opcode[5]), .F1(Opcode[4]),
    .Output(Result[7]), .Carry_Out(CF), .Carry_In(n1bit_alu_7_carry_out));
  not not_1 (not_1_out, Result[4]);
  not not_2 (not_2_out, Result[7]);
  not not_3 (not_3_out, Result[6]);
  not not_4 (not_4_out, Result[5]);
  and and_1 (ZF, not_2_out, not_3_out, not_4_out, not_1_out, not_8_out, not_5_out, not_7_out, not_6_out);
  not not_5 (not_5_out, Result[2]);
  not not_6 (not_6_out, Result[0]);
  not not_7 (not_7_out, Result[1]);
  not not_8 (not_8_out, Result[3]);

  assign SF = Result[7];
endmodule

module Register_File (
  input  [1:0] Sr0,
  input  WE,
  input  [1:0] Sw,
  input  [1:0] Sr1,
  input  [7:0] Data_In,
  input  in_6,
  output [7:0] Data_Out_0,
  output [7:0] Data_Out_1
);

  wire demultiplexer_1_out0, demultiplexer_1_out1, demultiplexer_1_out2, demultiplexer_1_out3;
  wire [7:0] register_1_q, register_2_q, register_3_q, register_4_q;

  Demultiplexer #(.select(2), .enable("false")) demultiplexer_1 (
    .out0(demultiplexer_1_out0), .out1(demultiplexer_1_out1), .out2(demultiplexer_1_out2),
    .out3(demultiplexer_1_out3), .in(WE), .sel(Sw));
  Register register_1 (.D(Data_In), .en(demultiplexer_1_out0), .Q(register_1_q), .clk(in_6));  // open: clr
  Register register_2 (.D(Data_In), .en(demultiplexer_1_out1), .Q(register_2_q), .clk(in_6));  // open: clr
  Register register_3 (.D(Data_In), .en(demultiplexer_1_out2), .Q(register_3_q), .clk(in_6));  // open: clr
  Register register_4 (.D(Data_In), .en(demultiplexer_1_out3), .Q(register_4_q), .clk(in_6));  // open: clr
  Multiplexer #(.select(2), .width(8), .enable("false")) multiplexer_1 (
    .in0(register_1_q), .in1(register_2_q), .in2(register_3_q), .in3(register_4_q), .out(Data_Out_0),
    .sel(Sr0));
  Multiplexer #(.select(2), .width(8), .enable("false")) multiplexer_2 (
    .in0(register_1_q), .in1(register_2_q), .in2(register_3_q), .in3(register_4_q), .out(Data_Out_1),
    .sel(Sr1));
endmodule

module PC_IR (
  input  Clear,
  input  enable,
  input  Clock,
  input  [15:0] data_in,
  output [7:0] addr_out,
  output [7:0] instruction,
  output [7:0] immediate_value
);

  wire [7:0] adder_1_out;

  Register PC (.D(adder_1_out), .en(enable), .Q(addr_out), .clk(Clock), .clr(Clear));
  Register #(.width(16)) IR (.D(data_in), .en(enable), .Q({instruction, immediate_value}), .clk(Clock), .clr(Clear));
  Adder adder_1 (.a(8'h1), .b(addr_out), .out(adder_1_out), .cin(1'b0));  // open: cout
endmodule

module Control_Store (
  input  Clear,
  input  Enable,
  input  Clock,
  input  Clear_2,
  input  Chip_Select,
  input  Clock_2,
  input  Load_Data,
  output [7:0] Current_Addr,
  output [7:0] _8_bit_inst,
  output [7:0] _8_bit_imm_value,
  output out_11,
  output [1:0] r1,
  output [1:0] r2,
  output [5:0] Output
);

  wire and_1_out, and_2_out, and_3_out, and_4_out, and_5_out, and_6_out, and_8_out, and_9_out, not_2_out,
       not_3_out, not_4_out, not_5_out, not_6_out, not_7_out, not_8_out, not_9_out, not_10_out, not_11_out,
       not_12_out, not_13_out;
  wire [15:0] ram_1_data;

  PC_IR pc_ir_1 (
    .Clear(Clear), .enable(Enable), .Clock(Clock), .instruction(_8_bit_inst), .addr_out(Current_Addr),
    .data_in(ram_1_data), .immediate_value(_8_bit_imm_value));
  not not_1 (Output[5], _8_bit_inst[6]);
  not not_2 (not_2_out, _8_bit_inst[6]);
  not not_3 (not_3_out, _8_bit_inst[6]);
  not not_4 (not_4_out, _8_bit_inst[4]);
  not not_5 (not_5_out, _8_bit_inst[5]);
  not not_6 (not_6_out, _8_bit_inst[6]);
  not not_7 (not_7_out, _8_bit_inst[6]);
  not not_8 (not_8_out, _8_bit_inst[5]);
  not not_9 (not_9_out, _8_bit_inst[6]);
  not not_10 (not_10_out, _8_bit_inst[6]);
  not not_11 (not_11_out, _8_bit_inst[5]);
  not not_12 (not_12_out, _8_bit_inst[4]);
  not not_13 (not_13_out, _8_bit_inst[6]);
  or or_1 (Output[4], not_2_out, _8_bit_inst[4]);
  and and_1 (and_1_out, not_3_out, not_4_out);
  or or_2 (Output[3], and_1_out, and_2_out, and_3_out);
  and and_2 (and_2_out, _8_bit_inst[5], _8_bit_inst[4]);
  and and_3 (and_3_out, _8_bit_inst[6], not_5_out);
  and and_4 (and_4_out, not_6_out, _8_bit_inst[4]);
  and and_5 (and_5_out, not_7_out, _8_bit_inst[5]);
  or or_3 (Output[2], and_4_out, and_5_out, and_6_out);
  and and_6 (and_6_out, _8_bit_inst[6], not_8_out);
  and and_7 (Output[1], not_9_out, _8_bit_inst[4]);
  and and_8 (and_8_out, not_10_out, not_11_out, not_12_out);
  or or_4 (Output[0], and_8_out, and_9_out);
  and and_9 (and_9_out, not_13_out, _8_bit_inst[5], _8_bit_inst[4]);
  RAM #(.dataWidth(16)) ram_1 (
    .addr(Current_Addr), .data(ram_1_data), .sel(Chip_Select), .clk(Clock_2), .ld(Load_Data), .clr(Clear_2));

  assign out_11 = _8_bit_inst[7];
  assign r1 = _8_bit_inst[3:2];
  assign r2 = _8_bit_inst[1:0];

  // Notes on the sheet:
  //   Load RAM with program
  //   Enable the PC_IR chip
  //   Each time you clock 0-->1-->0
  //   Next instruction is loaded 
  //   Note: data can flow either direction - in or out of RAM
  //   We only need data flowing out of RAM
  //   Turn on Chip Select and Load Data
  //   Do Not Clock, it's used to move data into RAM
endmodule

module test (
  input  a,
  input  b,
  input  c,
  output f0,
  output f1,
  output ena,
  output enb,
  output inva,
  output inc
);

  wire and_1_out, and_2_out, and_3_out, and_4_out, and_5_out, and_6_out, and_8_out, and_9_out, not_2_out,
       not_3_out, not_4_out, not_5_out, not_6_out, not_7_out, not_8_out, not_9_out, not_10_out, not_11_out,
       not_12_out, not_13_out;

  not not_1 (f0, a);
  not not_2 (not_2_out, a);
  not not_3 (not_3_out, a);
  not not_4 (not_4_out, c);
  not not_5 (not_5_out, b);
  not not_6 (not_6_out, a);
  not not_7 (not_7_out, a);
  not not_8 (not_8_out, b);
  not not_9 (not_9_out, a);
  not not_10 (not_10_out, a);
  not not_11 (not_11_out, b);
  not not_12 (not_12_out, c);
  not not_13 (not_13_out, a);
  or or_1 (f1, not_2_out, c);
  and and_1 (and_1_out, not_3_out, not_4_out);
  and and_2 (and_2_out, b, c);
  and and_3 (and_3_out, a, not_5_out);
  and and_4 (and_4_out, not_6_out, c);
  and and_5 (and_5_out, not_7_out, b);
  and and_6 (and_6_out, a, not_8_out);
  and and_7 (inva, not_9_out, c);
  and and_8 (and_8_out, not_10_out, not_11_out, not_12_out);
  and and_9 (and_9_out, not_13_out, b, c);
  or or_2 (ena, and_1_out, and_2_out, and_3_out);
  or or_3 (enb, and_4_out, and_5_out, and_6_out);
  or or_4 (inc, and_8_out, and_9_out);
endmodule

module clock1 (
  input  clock,
  output F,
  output D,
  output E,
  output W
);

  wire not_1_out, not_2_out, not_3_out, not_4_out, not_5_out;

  not not_1 (not_1_out, clock);
  not not_2 (not_2_out, clock);
  not not_3 (not_3_out, not_1_out);
  not not_4 (not_4_out, clock);
  not not_5 (not_5_out, not_1_out);
  and and_1 (F, not_2_out, not_3_out);
  and and_2 (D, not_4_out, not_1_out);
  and and_3 (E, clock, not_5_out);
  and and_4 (W, clock, not_1_out);
endmodule
